// Logisim project tragamonedas.circ as structural Verilog: 4 circuits, main circuit main
module main (
  input  [1:0] in_1,
  output out_2
);

  wire clock_1_out, Controlador_Palanca_influye;
  wire [1:0] counter_1_q, joystick_1_y;
  wire [6:0] imagerom_1_out_2, imagerom_1_out_3, imagerom_1_out_4, imagerom_1_out_5, imagerom_1_out_6,
       imagerom_2_out_2, imagerom_2_out_3, imagerom_2_out_4, imagerom_2_out_5, imagerom_2_out_6,
       imagerom_3_out_2, imagerom_3_out_3, imagerom_3_out_4, imagerom_3_out_5, imagerom_3_out_6;

  Joystick #(.bits(2)) joystick_1 (.y(joystick_1_y));  // open: x
  Counter #(.width(2), .max('h3)) counter_1 (.Q(counter_1_q), .clk(clock_1_out));  // open: load, D, count, carry, clr
  Clock clock_1 (.out(clock_1_out));
  // Probe on joystick_1_y
  DotMatrix dotmatrix_1 (
    .col0(imagerom_1_out_2), .col1(imagerom_1_out_3), .col2(imagerom_1_out_4), .col3(imagerom_1_out_5),
    .col4(imagerom_1_out_6));
  DotMatrix dotmatrix_2 (
    .col0(imagerom_2_out_2), .col1(imagerom_2_out_3), .col2(imagerom_2_out_4), .col3(imagerom_2_out_5),
    .col4(imagerom_2_out_6));
  ImageROM imagerom_1 (
    .in_1(counter_1_q), .out_2(imagerom_1_out_2), .out_3(imagerom_1_out_3), .out_4(imagerom_1_out_4),
    .out_5(imagerom_1_out_5), .out_6(imagerom_1_out_6));
  ImageROM imagerom_2 (
    .in_1(counter_1_q), .out_2(imagerom_2_out_2), .out_3(imagerom_2_out_3), .out_4(imagerom_2_out_4),
    .out_5(imagerom_2_out_5), .out_6(imagerom_2_out_6));
  controlador_palanca Controlador_Palanca (
    .Estado_de_Juego(in_1), .Palanca(joystick_1_y), .Influye(Controlador_Palanca_influye),
    .Activacion_Palanca(out_2));
  DotMatrix dotmatrix_3 (
    .col0(imagerom_3_out_2), .col1(imagerom_3_out_3), .col2(imagerom_3_out_4), .col3(imagerom_3_out_5),
    .col4(imagerom_3_out_6));
  ImageROM imagerom_3 (
    .in_1(counter_1_q), .out_2(imagerom_3_out_2), .out_3(imagerom_3_out_3), .out_4(imagerom_3_out_4),
    .out_5(imagerom_3_out_5), .out_6(imagerom_3_out_6));
  LED Influye (.in(Controlador_Palanca_influye));
  LED \Detección_Palanca  (.in(out_2));

  // Notes on the sheet:
  //   Harcodeado estado 11 = estado espera
endmodule

module ImageROM (
  input  [1:0] in_1,
  output [6:0] out_2,
  output [6:0] out_3,
  output [6:0] out_4,
  output [6:0] out_5,
  output [6:0] out_6
);

  ROM #(.addrWidth(2), .dataWidth(7)) rom_1 (.addr(in_1), .data(out_2));  // open: sel
  ROM #(.addrWidth(2), .dataWidth(7)) rom_2 (.addr(in_1), .data(out_3));  // open: sel
  ROM #(.addrWidth(2), .dataWidth(7)) rom_3 (.addr(in_1), .data(out_4));  // open: sel
  ROM #(.addrWidth(2), .dataWidth(7)) rom_4 (.addr(in_1), .data(out_5));  // open: sel
  ROM #(.addrWidth(2), .dataWidth(7)) rom_5 (.addr(in_1), .data(out_6));  // open: sel

  // Notes on the sheet:
  //   contents of rom_1 (hex, n*v repeats v):
  //   40 6 8
  //   contents of rom_2 (hex, n*v repeats v):
  //   43 3e 1b
  //   contents of rom_3 (hex, n*v repeats v):
  //   4c 7f 3e
  //   contents of rom_4 (hex, n*v repeats v):
  //   58 3e 6c
  //   contents of rom_5 (hex, n*v repeats v):
  //   60 6 8
endmodule

module controlador_palanca (
  input  [1:0] Estado_de_Juego,
  input  [1:0] Palanca,
  output Influye,
  output Activacion_Palanca
);

  wire and_2_out;

  and and_1 (Influye, Estado_de_Juego[0], Estado_de_Juego[1]);
  and and_2 (and_2_out, Palanca[0], Palanca[1]);
  and and_3 (Activacion_Palanca, Influye, and_2_out);
endmodule

module maquina_de_estados (
  input  Evento_Entrada,
  output A,
  output B
);

  wire and_1_out, and_2_out, clock_1_out, not_1_out;

  not not_1 (not_1_out, A);
  and and_1 (and_1_out, not_1_out, B, Evento_Entrada);
  and and_2 (and_2_out, Evento_Entrada, not_1_out);
  Clock clock_1 (.out(clock_1_out));
  D_Flip_Flop QA (.clk(clock_1_out), .D(and_1_out), .Q(A));  // open: Qn, preset, en, reset
  D_Flip_Flop QB (.clk(clock_1_out), .D(and_2_out), .Q(B));  // open: Qn, preset, en, reset
endmodule
